// Digital circuit core.dig as structural Verilog
module core (
  input  rst_n,
  input  CLK
);

  wire u_alu_zero, u_ctrl_branch, u_ctrl_jump, u_ctrl_reg_wen, u_pc_reg_ena;
  wire [1:0] u_ctrl_alu_src_sel;
  wire [2:0] u_ctrl_imm_gen_op;
  wire [4:0] u_ctrl_alu_op, u_ctrl_reg1_raddr, u_ctrl_reg2_raddr, u_ctrl_reg_waddr;
  wire [31:0] curr_pc, inst, next_pc, u_alu_alu_res, u_imm_gen_imm, u_mux_alu_alu_src1, u_mux_alu_alu_src2,
       u_regs_reg1_rdata, u_regs_reg2_rdata;

  // Probe on curr_pc
  // Probe on next_pc
  // Probe on inst
  mux_pc #(.applicationType("IVERILOG"), .iverilogOptions("-I D:/RISCV/myriscv_v2/src/core"), .CodeFile("D:\\RISCV\\myriscv_v2\\src\\core\\mux_pc.v")) u_mux_pc (
    .ena(u_pc_reg_ena), .curr_pc_i(curr_pc), .branch(u_ctrl_branch), .jump(u_ctrl_jump), .zero(u_alu_zero),
    .imm(u_imm_gen_imm), .next_pc_o(next_pc));
  inst_mem #(.applicationType("IVERILOG"), .iverilogOptions("-I D:/RISCV/myriscv_v2/src/core"), .CodeFile("D:\\RISCV\\myriscv_v2\\src\\core\\inst_mem.v")) u_inst_mem (
    .clk(CLK), .pc_addr_i(curr_pc), .inst_o(inst));
  pc_reg #(.applicationType("IVERILOG"), .iverilogOptions("-I D:/RISCV/myriscv_v2/src/core"), .CodeFile("D:\\RISCV\\myriscv_v2\\src\\core\\pc_reg.v")) u_pc_reg (
    .clk(CLK), .rst_n(rst_n), .rst_pc({32{1'b0}}), .next_pc_i(next_pc), .curr_pc_o(curr_pc),
    .ena(u_pc_reg_ena));
  ctrl #(.applicationType("IVERILOG"), .iverilogOptions("-I D:/RISCV/myriscv_v2/src/core"), .CodeFile("D:\\RISCV\\myriscv_v2\\src\\core\\ctrl.v")) u_ctrl (
    .inst(inst), .branch(u_ctrl_branch), .jump(u_ctrl_jump), .reg_wen(u_ctrl_reg_wen),
    .reg_waddr(u_ctrl_reg_waddr), .reg1_raddr(u_ctrl_reg1_raddr), .reg2_raddr(u_ctrl_reg2_raddr),
    .imm_gen_op(u_ctrl_imm_gen_op), .alu_op(u_ctrl_alu_op), .alu_src_sel(u_ctrl_alu_src_sel));  // open: regs_src_sel, mem_access_type, mem_sign_ext
  mux_alu #(.applicationType("IVERILOG"), .iverilogOptions("-I D:/RISCV/myriscv_v2/src/core"), .CodeFile("D:\\RISCV\\myriscv_v2\\src\\core\\mux_alu.v")) u_mux_alu (
    .alu_src_sel(u_ctrl_alu_src_sel), .reg1_rdata(u_regs_reg1_rdata), .reg2_rdata(u_regs_reg2_rdata),
    .imm(u_imm_gen_imm), .curr_pc(curr_pc), .alu_src1(u_mux_alu_alu_src1), .alu_src2(u_mux_alu_alu_src2));
  imm_gen #(.applicationType("IVERILOG"), .iverilogOptions("-I D:/RISCV/myriscv_v2/src/core"), .CodeFile("D:\\RISCV\\myriscv_v2\\src\\core\\imm_gen.v")) u_imm_gen (
    .inst(inst), .imm_gen_op(u_ctrl_imm_gen_op), .imm(u_imm_gen_imm));
  alu #(.applicationType("IVERILOG"), .iverilogOptions("-I D:/RISCV/myriscv_v2/src/core"), .CodeFile("D:\\RISCV\\myriscv_v2\\src\\core\\alu.v")) u_alu (
    .alu_op(u_ctrl_alu_op), .alu_src1(u_mux_alu_alu_src1), .alu_src2(u_mux_alu_alu_src2), .zero(u_alu_zero),
    .alu_res(u_alu_alu_res));
  regs #(.applicationType("IVERILOG"), .iverilogOptions("-I D:/RISCV/myriscv_v2/src/core"), .CodeFile("D:\\RISCV\\myriscv_v2\\src\\core\\regs.v")) u_regs (
    .clk(CLK), .rst_n(rst_n), .reg_wen(u_ctrl_reg_wen), .reg_waddr(u_ctrl_reg_waddr),
    .reg_wdata(u_alu_alu_res), .reg1_raddr(u_ctrl_reg1_raddr), .reg2_raddr(u_ctrl_reg2_raddr),
    .reg1_rdata(u_regs_reg1_rdata), .reg2_rdata(u_regs_reg2_rdata));
endmodule
