// Digital circuit pc.dig as structural Verilog
module pc (
  input  clk,
  input  rst_n
);

  wire [31:0] pc, pc_plus_4;

  // Probe on pc
  // Probe on pc_plus_4
  pc_reg #(.applicationType("IVERILOG"), .iverilogOptions_File("D:\\RISCV\\myriscv_v2\\src\\core\\defines.v")) u_pc_reg (
    .clk(clk), .rst_n(rst_n), .rst_pc(32'h4000000), .next_pc_i(pc_plus_4), .curr_pc_o(pc));  // open: ena
  pc_4 #(.applicationType("IVERILOG")) u_pc_4 (.din(pc), .dout(pc_plus_4));
  regs #(.applicationType("IVERILOG")) u_regs ();  // open: clk, rst_n, reg_wen, reg_waddr, reg_wdata, reg1_raddr, reg2_raddr, reg1_rdata, reg2_rdata
endmodule

/* Code of pc_reg:
/* -------程序计数器模块-------- * /



module pc_reg (
    input   wire                        clk         ,
    input   wire                        rst_n       ,
    input   wire    [`CPU_WIDTH - 1:0]  rst_pc      ,
    output  reg                         ena         ,
    input   wire    [`CPU_WIDTH - 1:0]  next_pc_i   ,   // 下一个程序计数器地址
    output  reg     [`CPU_WIDTH - 1:0]  curr_pc_o       // 当前程序计数器地址

);
//ena:系统使能信号
always @(posedge clk or negedge rst_n) begin
    if (!rst_n) begin
        ena <= 1'b0;
    end
    else begin
        ena <= 1'b1;
    end
end

//curr_pc_o:当前程序计数器输出
always @(posedge clk or negedge rst_n) begin
    if (!rst_n) begin
        curr_pc_o <= rst_pc; //复位时，回到复位地址的指令
    end
    else begin
        curr_pc_o <= next_pc_i;     
    end

end
endmodule
*/

/* Code of pc_4:
module pc_4(
 	input [31:0] din,
	output [31:0] dout
);
	assign dout = din +32'd4;
endmodule
*/

/* Code of regs:
/* -------寄存器堆模块-------- * /

//`include "defines.v"

`define CPU_WIDTH               32
`define REG_DATA_DEPTH 32
`define REG_ADDR_WIDTH 5 // 2^5 = 32

module regs (
    input                            clk,
    input                            rst_n,

    input                            reg_wen,    // 寄存器写使能
    input      [`REG_ADDR_WIDTH-1:0] reg_waddr,  // 寄存器写地址
    input      [`CPU_WIDTH-1:0]      reg_wdata,  // 寄存器写数据

    input      [`REG_ADDR_WIDTH-1:0] reg1_raddr, // 寄存器1读地址
    input      [`REG_ADDR_WIDTH-1:0] reg2_raddr, // 寄存器2读地址
    output reg [`CPU_WIDTH-1:0]      reg1_rdata, // 寄存器1读数据
    output reg [`CPU_WIDTH-1:0]      reg2_rdata  // 寄存器2读数据
);
    
reg [`CPU_WIDTH-1:0] regs [0:`REG_DATA_DEPTH-1]; 

// register write
always @(posedge clk or negedge rst_n) begin
    if (rst_n && reg_wen && (reg_waddr != `REG_ADDR_WIDTH'b0)) // x0 read only
        regs[reg_waddr] <= reg_wdata; 
end

// register 1 read
always @(*) begin
    if(reg1_raddr == `REG_ADDR_WIDTH'b0)
        reg1_rdata = `CPU_WIDTH'b0;
    else
        reg1_rdata = regs[reg1_raddr];
end

// register 2 read
always @(*) begin
    if(reg2_raddr == `REG_ADDR_WIDTH'b0)
        reg2_rdata = `CPU_WIDTH'b0;
    else
        reg2_rdata = regs[reg2_raddr];
end


endmodule
*/
